# Fritzing sketch mcslck (saved by Fritzing 0.8.5b)
circuit board: 5cm x 2cm
breadboards: 1

parts:
  USB = USB Connectors [package=usb-a-pcb]
  C4 = 0603-X
  IC1 = LQFP-48 [chip_label=IC package=LQFP]
  C5 = 0603-X
  0603-X4 = 0603-X
  22R = 0603-X
  C1 = Ceramic Capacitor [capacitance=2.2µF package="0603 [SMD, multilayer]"]
  C6 = 0603-X
  C3 = 0603-X
  LED = 0603-X
  5R2 = 0603-X
  BD = 0603-X
  C7 = 0603-X
  S1 = SWITCH-MOMENTARY-2 [package=tactile-switch-1101ne]
  J8 = female pin header, 4 pins [form="♀ (female)"]
  J11 = female pin header, 2 pins [form="♀ (female)"]
  C8 = 0603-X
  J22 = female alternating pin header, 1 pin [form="♀ (female)"]
  J23 = female alternating pin header, 1 pin [form="♀ (female)"]
  J5 = female alternating pin header, 10 pins [form="♀ (female)"]
  J21 = female alternating pin header, 1 pin [form="♀ (female)"]
  J25 = female pin header, 1 pin [form="♀ (female)"]
  J26 = female pin header, 1 pin [form="♀ (female)"]
  J31 = female pin header, 1 pin [form="♀ (female)"]
  J32 = female pin header, 1 pin [form="♀ (female)"]
  J36 = female pin header, 1 pin [form="♀ (female)"]
  J28 = female alternating pin header, 1 pin [form="♀ (female)"]
  J29 = female alternating pin header, 1 pin [form="♀ (female)"]
  J27 = female alternating pin header, 1 pin [form="♀ (female)"]
  J19 = female alternating pin header, 1 pin [form="♀ (female)"]
  J33 = female alternating pin header, 1 pin [form="♀ (female)"]
  J35 = female alternating pin header, 1 pin [form="♀ (female)"]
  J30 = female alternating pin header, 1 pin [form="♀ (female)"]
  J24 = female alternating pin header, 1 pin [form="♀ (female)"]
  J34 = female alternating pin header, 1 pin [form="♀ (female)"]
  J14 = female alternating pin header, 1 pin [form="♀ (female)"]
  J18 = female alternating pin header, 1 pin [form="♀ (female)"]
  Cut-away = Pad [width=10 height=2.5 connect=center]  # not connected
  Cut-away_2 = Pad [width=10 height=3.7 connect=center]  # not connected
  C2 = Ceramic Capacitor [capacitance=2.2µF package="0603 [SMD, multilayer]"]
  J4 = female pin header, 7 pins [form="♀ (female)"]
  C9 = 0603-X

nets:
  N1: USB.VBUS, BD.PIN2
  N2: USB.GND, C4.PIN1, IC1.2, IC1.11, IC1.12, IC1.23, C5.PIN2, C1.1, C6.PIN2, C3.PIN1, 5R2.PIN2, C7.PIN2, S1.1, J8.pin2, C8.PIN1, J5.pin2, J5.pin10, C2.1, J4.pin3, C9.PIN1
  N3: USB.D-, 22R.PIN2
  N4: USB.D+, 0603-X4.PIN2
  N5: C4.PIN2, IC1.1, IC1.5, IC1.9, IC1.10, IC1.16, IC1.22, C5.PIN1, C1.0, C6.PIN1, J35.pin1, J4.pin2
  N6: IC1.3, 0603-X4.PIN1, J4.pin4
  N7: IC1.4, 22R.PIN1, J4.pin5
  N8: IC1.6, BD.PIN1, C2.0, J4.pin6
  N9: IC1.7, J4.pin7
  N10: IC1.8, J5.pin1
  N11: IC1.13, C3.PIN2, J23.pin1
  N12: IC1.14, J19.pin1
  N13: IC1.15, J5.pin3
  N14: IC1.17, J5.pin4
  N15: IC1.18, J5.pin5
  N16: IC1.19, J5.pin6
  N17: IC1.20, J5.pin7
  N18: IC1.21, J5.pin8
  N19: IC1.24, C7.PIN1, J5.pin9
  N20: IC1.25, C8.PIN2, J18.pin1
  N21: IC1.26, S1.2, C9.PIN2
  N22: IC1.27, J14.pin1
  N23: IC1.28, J11.pin2
  N24: IC1.29, J11.pin1
  N25: IC1.30, J21.pin1
  N26: IC1.31, LED.PIN2
  N27: IC1.32, J8.pin4
  N28: IC1.33, J8.pin3
  N29: IC1.34, J22.pin1
  N30: IC1.35, J8.pin1
  N31: IC1.36, J36.pin1
  N32: IC1.37, J34.pin1
  N33: IC1.38, J33.pin1
  N34: IC1.39, J32.pin1
  N35: IC1.40, J31.pin1
  N36: IC1.41, J30.pin1
  N37: IC1.42, J29.pin1
  N38: IC1.43, J28.pin1
  N39: IC1.44, J27.pin1
  N40: IC1.45, J26.pin1
  N41: IC1.46, J25.pin1
  N42: IC1.47, J24.pin1
  N43: IC1.48, J4.pin1
  N44: LED.PIN1, 5R2.PIN1

custom parts:
  0603-X: Landing pad with extra space
